// Logisim project 8_bit_CPU.circ as structural Verilog: 5 circuits, main circuit main
module main (
  output [7:0] out_1,
  output [7:0] out_2,
  output [15:0] out_3,
  output [7:0] out_4,
  output [7:0] out_5
);

  wire button_1_out, button_2_out, button_3_out, button_4_out, clock_1_out, d_ff_1_q, d_ff_1_qn, d_ff_2_q,
       d_ff_2_qn, d_ff_3_q, d_ff_3_qn, d_ff_4_q, d_ff_4_qn, d_ff_5_q, d_ff_5_qn, d_ff_6_q, d_ff_6_qn,
       nand_1_out, not_1_out, not_2_out, not_3_out, register_8bit_3_borrow, register_8bit_3_carry, RESET_out,
       undriven;
  wire [0:0] or_1_out;
  wire [7:0] ring_counter_1_q, rom_1_data;

  Button #(.press("passive")) button_1 (.out(button_1_out));
  not not_1 (not_1_out, button_1_out);
  nand nand_1 (nand_1_out, button_1_out, not_1_out);
  Button #(.press("passive")) button_2 (.out(button_2_out));
  Button #(.press("passive")) button_3 (.out(button_3_out));
  Button #(.press("passive")) button_4 (.out(button_4_out));
  Clock clock_1 (.out(clock_1_out));
  Button RESET (.out(RESET_out));
  register_8bit register_8bit_1 (
    .DATA(8'h12), .NOT_WRITE(1'b1), .RESET(RESET_out), .INC(register_8bit_3_carry),
    .DEC(register_8bit_3_borrow), .Q(out_3[15:8]));  // open: CARRY, BORROW
  register_8bit register_8bit_2 (
    .DATA(8'h80), .NOT_WRITE(button_2_out), .INC(button_3_out), .DEC(button_4_out), .Q(out_5));  // open: RESET, CARRY, BORROW
  register_8bit register_8bit_3 (
    .DATA(8'h34), .NOT_WRITE(1'b1), .RESET(RESET_out), .INC(1'b1), .DEC(1'b1), .Q(out_3[7:0]),
    .CARRY(register_8bit_3_carry), .BORROW(register_8bit_3_borrow));
  RAM ram_1 ();  // open: addr, we, oe, clk, din, dout
  ring_counter ring_counter_1 (.CLK(clock_1_out), .RESET(RESET_out), .Q(ring_counter_1_q));
  ROM #(.addrWidth(17)) rom_1 (.addr({out_3, or_1_out[0]}), .data(rom_1_data));
  or or_1 (or_1_out[0], ring_counter_1_q[5], ring_counter_1_q[4]);
  D_Flip_Flop d_ff_1 (.D(d_ff_1_qn), .Q(d_ff_1_q), .Qn(d_ff_1_qn), .reset(undriven));  // open: clk, preset
  adder_subtractor_8bit adder_subtractor_8bit_1 (.A(8'h4), .B({8{1'b1}}), .Q(out_4));  // open: ADD_SUB, C_OUT
  D_Flip_Flop d_ff_2 (.D(d_ff_2_qn), .clk(d_ff_1_qn), .Q(d_ff_2_q), .Qn(d_ff_2_qn), .reset(undriven));  // open: preset
  not not_2 (not_2_out, ring_counter_1_q[6]);
  not not_3 (not_3_out, ring_counter_1_q[4]);
  D_Flip_Flop d_ff_3 (.D(d_ff_3_qn), .clk(d_ff_2_qn), .Q(d_ff_3_q), .Qn(d_ff_3_qn), .reset(undriven));  // open: preset
  D_Flip_Flop d_ff_4 (.D(d_ff_4_qn), .clk(d_ff_3_qn), .Q(d_ff_4_q), .Qn(d_ff_4_qn), .reset(undriven));  // open: preset
  D_Flip_Flop d_ff_5 (.D(d_ff_5_qn), .clk(d_ff_4_qn), .Q(d_ff_5_q), .Qn(d_ff_5_qn), .reset(undriven));  // open: preset
  register_8bit ACCUMULATOR ();  // open: DATA, NOT_WRITE, RESET, INC, DEC, Q, CARRY, BORROW
  register_8bit OPCODE_REGISTER (
    .DATA(rom_1_data), .NOT_WRITE(not_2_out), .RESET(RESET_out), .Q(out_1));  // open: INC, DEC, CARRY, BORROW
  register_8bit OPERAND_REGISTER (
    .DATA(rom_1_data), .NOT_WRITE(not_3_out), .RESET(RESET_out), .Q(out_2));  // open: INC, DEC, CARRY, BORROW
  D_Flip_Flop d_ff_6 (.D(d_ff_6_qn), .clk(d_ff_5_qn), .Q(d_ff_6_q), .Qn(d_ff_6_qn), .reset(undriven));  // open: preset

  // Notes on the sheet:
  //   PROGRAM COUNTER
  //   contents of rom_1 (hex, n*v repeats v):
  //   1 2
endmodule

module register_8bit (
  input  [7:0] DATA,
  input  NOT_WRITE,
  input  RESET,
  input  INC,
  input  DEC,
  output [7:0] Q,
  output CARRY,
  output BORROW
);

  wire n74193_1_pin4, n74193_1_pin5;

  _74193 #(.ShowInternalStructure("true")) u_74193_1 (
    .pin1(DATA[5]), .pin2(Q[5]), .pin3(Q[4]), .pin4(n74193_1_pin4), .pin5(n74193_1_pin5), .pin6(Q[6]),
    .pin7(Q[7]), .pin15(DATA[4]), .pin14(RESET), .pin13(BORROW), .pin12(CARRY), .pin11(NOT_WRITE),
    .pin10(DATA[6]), .pin9(DATA[7]));
  _74193 #(.ShowInternalStructure("true")) u_74193_2 (
    .pin1(DATA[1]), .pin2(Q[1]), .pin3(Q[0]), .pin4(DEC), .pin5(INC), .pin6(Q[2]), .pin7(Q[3]),
    .pin15(DATA[0]), .pin14(RESET), .pin13(n74193_1_pin4), .pin12(n74193_1_pin5), .pin11(NOT_WRITE),
    .pin10(DATA[2]), .pin9(DATA[3]));
endmodule

module ring_counter (
  input  CLK,
  input  RESET,
  output [7:0] Q
);

  wire nor_1_out, or_1_out, or_2_out, or_3_out, or_4_out, or_5_out, or_6_out;

  D_Flip_Flop d_ff_1 (.D(Q[0]), .clk(CLK), .Q(Q[7]), .preset(nor_1_out), .reset(RESET));  // open: Qn
  or or_1 (or_1_out, Q[7], Q[6]);
  D_Flip_Flop d_ff_2 (.D(Q[7]), .clk(CLK), .Q(Q[6]), .reset(RESET));  // open: Qn, preset
  or or_2 (or_2_out, or_1_out, or_3_out);
  D_Flip_Flop d_ff_3 (.D(Q[6]), .clk(CLK), .Q(Q[5]), .reset(RESET));  // open: Qn, preset
  D_Flip_Flop d_ff_4 (.D(Q[5]), .clk(CLK), .Q(Q[4]), .reset(RESET));  // open: Qn, preset
  nor nor_1 (nor_1_out, or_2_out, or_5_out);
  or or_3 (or_3_out, Q[5], Q[4]);
  D_Flip_Flop d_ff_5 (.D(Q[4]), .clk(CLK), .Q(Q[3]), .reset(RESET));  // open: Qn, preset
  or or_4 (or_4_out, Q[3], Q[2]);
  D_Flip_Flop d_ff_6 (.D(Q[3]), .clk(CLK), .Q(Q[2]), .reset(RESET));  // open: Qn, preset
  or or_5 (or_5_out, or_4_out, or_6_out);
  D_Flip_Flop d_ff_7 (.D(Q[2]), .clk(CLK), .Q(Q[1]), .reset(RESET));  // open: Qn, preset
  or or_6 (or_6_out, Q[1], Q[0]);
  D_Flip_Flop d_ff_8 (.D(Q[1]), .clk(CLK), .Q(Q[0]), .reset(RESET));  // open: Qn, preset
endmodule

module full_adder (
  input  A,
  input  B,
  input  C_IN,
  output Q,
  output C_OUT
);

  wire and_1_out, and_2_out, xor_1_out;

  xor xor_1 (xor_1_out, A, B);
  and and_1 (and_1_out, A, B);
  xor xor_2 (Q, xor_1_out, C_IN);
  and and_2 (and_2_out, xor_1_out, C_IN);
  or or_1 (C_OUT, and_2_out, and_1_out);
endmodule

module adder_subtractor_8bit (
  input  [7:0] A,
  input  [7:0] B,
  input  ADD_SUB,
  output [7:0] Q,
  output C_OUT
);

  wire full_adder_2_c_out, full_adder_3_c_out, full_adder_4_c_out, full_adder_5_c_out, full_adder_6_c_out,
       full_adder_7_c_out, full_adder_8_c_out, xor_1_out, xor_2_out, xor_3_out, xor_4_out, xor_5_out,
       xor_6_out, xor_7_out, xor_8_out;

  xor xor_1 (xor_1_out, B[7], ADD_SUB);
  xor xor_2 (xor_2_out, B[6], ADD_SUB);
  full_adder full_adder_1 (.A(A[7]), .B(xor_1_out), .C_IN(full_adder_2_c_out), .Q(Q[7]), .C_OUT(C_OUT));
  xor xor_3 (xor_3_out, B[5], ADD_SUB);
  full_adder full_adder_2 (.A(A[6]), .B(xor_2_out), .C_IN(full_adder_3_c_out), .Q(Q[6]), .C_OUT(full_adder_2_c_out));
  full_adder full_adder_3 (.A(A[5]), .B(xor_3_out), .C_IN(full_adder_4_c_out), .Q(Q[5]), .C_OUT(full_adder_3_c_out));
  xor xor_4 (xor_4_out, B[4], ADD_SUB);
  xor xor_5 (xor_5_out, B[3], ADD_SUB);
  full_adder full_adder_4 (.A(A[4]), .B(xor_4_out), .C_IN(full_adder_5_c_out), .Q(Q[4]), .C_OUT(full_adder_4_c_out));
  full_adder full_adder_5 (.A(A[3]), .B(xor_5_out), .C_IN(full_adder_6_c_out), .Q(Q[3]), .C_OUT(full_adder_5_c_out));
  xor xor_6 (xor_6_out, B[2], ADD_SUB);
  xor xor_7 (xor_7_out, B[1], ADD_SUB);
  full_adder full_adder_6 (.A(A[2]), .B(xor_6_out), .C_IN(full_adder_7_c_out), .Q(Q[2]), .C_OUT(full_adder_6_c_out));
  full_adder full_adder_7 (.A(A[1]), .B(xor_7_out), .C_IN(full_adder_8_c_out), .Q(Q[1]), .C_OUT(full_adder_7_c_out));
  xor xor_8 (xor_8_out, B[0], ADD_SUB);
  full_adder full_adder_8 (.A(A[0]), .B(xor_8_out), .C_IN(ADD_SUB), .Q(Q[0]), .C_OUT(full_adder_8_c_out));
endmodule
